// Logisim project my_simple_risc_cpu.circ as structural Verilog: 4 circuits, main circuit Register_File
module main (
  input  [15:0] in_1,
  output [31:0] instruction,
  output [31:0] out_3,
  output [23:0] Branch_Target,
  output [31:0] data_to_write,
  output [31:0] op1,
  output [31:0] op2,
  output [31:0] out_8,
  output [31:0] out_9
);

  wire and_1_out, and_2_out, clock, E, GT, isAdd, isAnd, isAsr, isBeq, isBgt, isBranchTaken, isCall, isCmp,
       isDiv, isImmediate, isLoad, isLsl, isLsr, isMod, isMov, isMul, isNot, isOr, isRet, isStore, isSub,
       isUbranch, isWb, not_1_out, or_2_out, reset;
  wire [3:0] multiplexer_6_out, multiplexer_7_out, multiplexer_8_out;
  wire [23:0] adder_1_out, adder_2_out, multiplexer_4_out, PC;
  wire [31:0] bit_extender_1_out, bit_extender_2_out, multiplexer_1_out;

  Clock clock_1 (.out(clock));
  Button button_1 (.out(reset));
  Adder #(.width(24)) adder_1 (.a(PC), .b(24'h1), .out(adder_1_out));  // open: cin, cout
  Multiplexer #(.width(32)) multiplexer_1 (
    .in0(op2), .in1(out_3), .out(multiplexer_1_out), .sel(isImmediate));  // open: en
  Counter #(.width(24), .max('hffffff), .trigger("falling")) u_PC (
    .load(isBranchTaken), .D(multiplexer_4_out), .count(not_1_out), .Q(PC), .clk(clock), .clr(reset));  // open: carry
  not not_1 (not_1_out, isBranchTaken);
  Adder #(.width(24)) adder_2 (.a(PC), .b(instruction[23:0]), .out(adder_2_out), .cin(1'b1));  // open: cout
  assign bit_extender_1_out = {{8{1'b0}}, adder_1_out};  // Bit_Extender bit_extender_1
  assign bit_extender_2_out = {{16{instruction[15]}}, instruction[15:0]};  // Bit_Extender bit_extender_2
  Multiplexer #(.width(24), .enable("false")) multiplexer_2 (
    .in0(adder_2_out), .in1(op1[23:0]), .out(Branch_Target), .sel(isRet));
  Multiplexer #(.select(2), .width(32)) multiplexer_3 (
    .in0(out_9), .in1(out_8), .in2(bit_extender_1_out), .out(data_to_write), .sel({isCall, isLoad}));  // open: in3, en
  ALU ALU (
    .A(op1), .B(multiplexer_1_out), .isAdd(isAdd), .isSub(isSub), .isCmp(isCmp), .isMul(isMul),
    .isDiv(isDiv), .isMod(isMod), .isLsl(isLsl), .isLsr(isLsr), .isAsr(isAsr), .isOr(isOr), .isAnd(isAnd),
    .isNot(isNot), .isMov(isMov), .GT(GT), .E(E), .clock(clock), .aluResult(out_9));
  Multiplexer #(.width(24), .enable("false")) multiplexer_4 (
    .in0(PC), .in1(Branch_Target), .out(multiplexer_4_out), .sel(isBranchTaken));
  Multiplexer #(.select(2), .width(32), .enable("false")) multiplexer_5 (
    .in0(bit_extender_2_out), .in1({in_1, instruction[15:0]}), .in2({instruction[15:0], in_1}), .out(out_3),
    .sel(instruction[17:16]));  // open: in3
  ROM #(.addrWidth(24), .dataWidth(32)) rom_1 (.addr(PC), .data(instruction));  // open: sel
  Multiplexer #(.width(4)) multiplexer_6 (
    .in0(instruction[21:18]), .in1(4'b1111), .out(multiplexer_6_out), .sel(isRet));  // open: en
  Multiplexer #(.width(4)) multiplexer_7 (
    .in0(instruction[17:14]), .in1(instruction[25:22]), .out(multiplexer_7_out), .sel(isStore));  // open: en
  Multiplexer #(.width(4)) multiplexer_8 (
    .in0(instruction[25:22]), .in1(4'b1111), .out(multiplexer_8_out), .sel(isCall));  // open: en
  and and_1 (and_1_out, isBeq, E);
  and and_2 (and_2_out, isBgt, GT);
  Register_File register_file_1 (
    .read_port_1(multiplexer_6_out), .read_port_2(multiplexer_7_out), .data_to_write(data_to_write),
    .write_port(multiplexer_8_out), .isWb(isWb), .clock(clock), .reset(reset), .op1(op1), .op2(op2));
  or or_1 (isBranchTaken, isUbranch, and_1_out, and_2_out);
  or or_2 (or_2_out, isLoad, isStore);
  RAM #(.addrWidth(24), .dataWidth(32), .bus("separate")) ram_1 (
    .addr(out_9[23:0]), .din(op2), .data(out_8), .str(isStore), .sel(or_2_out), .clk(clock), .ld(isLoad),
    .clr(reset));
  Control_Unit Control_Unit (
    .I(instruction[26]), .op1(instruction[27]), .op2(instruction[28]), .op3(instruction[29]),
    .op4(instruction[30]), .op5(instruction[31]), .isImmediate(isImmediate), .isAdd(isAdd),
    .isStore(isStore), .isLoad(isLoad), .isBeq(isBeq), .isBgt(isBgt), .isRet(isRet), .isCall(isCall),
    .isWb(isWb), .isUbranch(isUbranch), .isSub(isSub), .isCmp(isCmp), .isMul(isMul), .isDiv(isDiv),
    .isMod(isMod), .isLsl(isLsl), .isLsr(isLsr), .isAsr(isAsr), .isOr(isOr), .isAnd(isAnd), .isNot(isNot),
    .isMov(isMov));

  // Other names for the same wires on the sheet: aluResult[31:0] = out_9; BranchPC[23:0] = Branch_Target;
  //   immx[31:0] = out_3; imm[15:0] = instruction[15:0]; inst[23:0] = instruction[23:0];
  //   rs2[3:0] = instruction[17:14]; modifierBits[1:0] = instruction[17:16]; rs1[3:0] = instruction[21:18];
  //   rd[3:0] = instruction[25:22]; ldResult[31:0] = out_8; op1_inst[23:0] = op1[23:0]

  // Notes on the sheet:
  //   Instruction Fetch Unit
  //   Calculate Immediate
  //   contents of rom_1 (hex, n*v repeats v):
  //   90000010 2c000001 8000000c 88000001 9000000a fb80002 7c380000 7ff80001 c000001 9ffffff7 74380000
  //   77f80001 10404000 7b80002 a0000000 4c400001 a0000000 4c00000a 9fffffee
  //   Memory Unit
endmodule

// CU
module Control_Unit (
  input  I,
  input  op1,
  input  op2,
  input  op3,
  input  op4,
  input  op5,
  output isImmediate,
  output isAdd,
  output isStore,
  output isLoad,
  output isBeq,
  output isBgt,
  output isRet,
  output isCall,
  output isWb,
  output isUbranch,
  output isSub,
  output isCmp,
  output isMul,
  output isDiv,
  output isMod,
  output isLsl,
  output isLsr,
  output isAsr,
  output isOr,
  output isAnd,
  output isNot,
  output isMov
);

  wire and_1_out, and_2_out, and_9_out, not_1_out, not_2_out, not_3_out, not_4_out, not_5_out, not_6_out,
       not_7_out, not_8_out, not_9_out, not_10_out, not_11_out, not_12_out, not_13_out, not_14_out,
       not_15_out, not_16_out, not_17_out, not_18_out, not_19_out, not_20_out, not_21_out, not_22_out,
       not_23_out, not_24_out, not_25_out, not_26_out, not_27_out, not_28_out, not_29_out, not_30_out,
       not_31_out, not_32_out, not_33_out, not_34_out, not_35_out, not_36_out, not_37_out, not_38_out,
       not_39_out, not_40_out, not_41_out, not_42_out, not_43_out, not_44_out, not_45_out, not_46_out,
       not_47_out, not_48_out, not_49_out, not_50_out, not_51_out, not_52_out, not_53_out, not_54_out,
       not_55_out, not_56_out, not_57_out, not_58_out, not_59_out, not_60_out, not_61_out, not_62_out,
       not_63_out, not_64_out, not_65_out, or_1_out, or_2_out, or_3_out;

  not not_1 (not_1_out, op2);
  not not_2 (not_2_out, op5);
  not not_3 (not_3_out, op4);
  not not_4 (not_4_out, op3);
  not not_5 (not_5_out, op2);
  not not_6 (not_6_out, op1);
  not not_7 (not_7_out, op5);
  not not_8 (not_8_out, op5);
  not not_9 (not_9_out, op1);
  not not_10 (not_10_out, op4);
  not not_11 (not_11_out, op3);
  not not_12 (not_12_out, op2);
  not not_13 (not_13_out, op1);
  not not_14 (not_14_out, op4);
  not not_15 (not_15_out, op3);
  not not_16 (not_16_out, op2);
  not not_17 (not_17_out, op4);
  not not_18 (not_18_out, op2);
  not not_19 (not_19_out, op1);
  not not_20 (not_20_out, op4);
  not not_21 (not_21_out, op3);
  not not_22 (not_22_out, op5);
  or or_1 (or_1_out, op4, not_1_out);
  not not_23 (not_23_out, op4);
  not not_24 (not_24_out, op3);
  not not_25 (not_25_out, op1);
  not not_26 (not_26_out, op5);
  not not_27 (not_27_out, op4);
  not not_28 (not_28_out, op3);
  not not_29 (not_29_out, op2);
  not not_30 (not_30_out, op5);
  not not_31 (not_31_out, op4);
  not not_32 (not_32_out, op2);
  not not_33 (not_33_out, op5);
  not not_34 (not_34_out, op4);
  not not_35 (not_35_out, op3);
  not not_36 (not_36_out, op1);
  not not_37 (not_37_out, op5);
  not not_38 (not_38_out, op4);
  not not_39 (not_39_out, op3);
  not not_40 (not_40_out, op5);
  not not_41 (not_41_out, op4);
  not not_42 (not_42_out, op2);
  not not_43 (not_43_out, op1);
  not not_44 (not_44_out, op5);
  not not_45 (not_45_out, op3);
  not not_46 (not_46_out, op1);
  not not_47 (not_47_out, op5);
  not not_48 (not_48_out, op3);
  not not_49 (not_49_out, op5);
  not not_50 (not_50_out, op2);
  not not_51 (not_51_out, op1);
  not not_52 (not_52_out, op5);
  not not_53 (not_53_out, op4);
  not not_54 (not_54_out, op5);
  not not_55 (not_55_out, op4);
  not not_56 (not_56_out, op1);
  not not_57 (not_57_out, op5);
  not not_58 (not_58_out, op3);
  not not_59 (not_59_out, op2);
  not not_60 (not_60_out, op1);
  not not_61 (not_61_out, op5);
  not not_62 (not_62_out, op3);
  not not_63 (not_63_out, op2);
  and and_1 (and_1_out, not_22_out, op3, op1, or_1_out);
  and and_2 (and_2_out, not_2_out, not_3_out, not_4_out, not_5_out, not_6_out);
  and and_3 (isStore, not_7_out, op4, op3, op2, op1);
  or or_2 (or_2_out, isStore, isLoad);
  and and_4 (isLoad, not_8_out, op4, op3, op2, not_9_out);
  and and_5 (isBeq, op5, not_10_out, not_11_out, not_12_out, not_13_out);
  and and_6 (isBgt, op5, not_14_out, not_15_out, not_16_out, op1);
  and and_7 (isRet, op5, not_17_out, op3, not_18_out, not_19_out);
  and and_8 (isCall, op5, not_20_out, not_21_out, op2, op1);
  or or_3 (or_3_out, op5, and_1_out);
  and and_9 (and_9_out, op5, not_23_out, not_24_out, op2, not_25_out);
  and and_10 (isSub, not_26_out, not_27_out, not_28_out, not_29_out, op1);
  and and_11 (isCmp, not_30_out, not_31_out, op3, not_32_out, op1);
  and and_12 (isMul, not_33_out, not_34_out, not_35_out, op2, not_36_out);
  and and_13 (isDiv, not_37_out, not_38_out, not_39_out, op2, op1);
  and and_14 (isMod, not_40_out, not_41_out, op3, not_42_out, not_43_out);
  and and_15 (isLsl, not_44_out, op4, not_45_out, op2, not_46_out);
  and and_16 (isLsr, not_47_out, op4, not_48_out, op2, op1);
  and and_17 (isAsr, not_49_out, op4, op3, not_50_out, not_51_out);
  and and_18 (isOr, not_52_out, not_53_out, op3, op2, op1);
  and and_19 (isAnd, not_54_out, not_55_out, op3, op2, not_56_out);
  and and_20 (isNot, not_57_out, op4, not_58_out, not_59_out, not_60_out);
  and and_21 (isMov, not_61_out, op4, not_62_out, not_63_out, op1);
  not not_64 (not_64_out, op5);
  or or_4 (isAdd, and_2_out, or_2_out);
  not not_65 (not_65_out, or_3_out);
  and and_22 (isImmediate, I, not_64_out);
  or or_5 (isWb, isCall, not_65_out);
  or or_6 (isUbranch, isCall, isRet, and_9_out);
endmodule

// RegFile
module Register_File (
  input  [3:0] read_port_1,
  input  [3:0] read_port_2,
  input  [31:0] data_to_write,
  input  [3:0] write_port,
  input  isWb,
  input  clock,
  input  reset,
  output [31:0] op1,
  output [31:0] op2
);

  wire counter_1_q, enbR0, enbR1, enbR2, enbR3, enbR4, enbR5, enbR6, enbR7, enbR8, enbR9, enbR10, enbR11,
       enbR12, enbR13, enbR14, enbR15, not_1_out, or_1_out;
  wire [31:0] demultiplexer_1_out0, demultiplexer_1_out1, demultiplexer_1_out2, demultiplexer_1_out3,
       demultiplexer_1_out4, demultiplexer_1_out5, demultiplexer_1_out6, demultiplexer_1_out7,
       demultiplexer_1_out8, demultiplexer_1_out9, demultiplexer_1_out10, demultiplexer_1_out11,
       demultiplexer_1_out12, demultiplexer_1_out13, demultiplexer_1_out14, demultiplexer_1_out15,
       multiplexer_1_out, r0, r1, r2, r3, r4, r5, r6, r7, r8, r9, r10, r11, r12, r13, r14, r15;

  Decoder #(.select(4)) decoder_1 (
    .out0(enbR0), .out1(enbR1), .out2(enbR2), .out3(enbR3), .out4(enbR4), .out5(enbR5), .out6(enbR6),
    .out7(enbR7), .out8(enbR8), .out9(enbR9), .out10(enbR10), .out11(enbR11), .out12(enbR12), .out13(enbR13),
    .out14(enbR14), .out15(enbR15), .sel(write_port));  // open: en
  Demultiplexer #(.select(4), .width(32)) demultiplexer_1 (
    .out0(demultiplexer_1_out0), .out1(demultiplexer_1_out1), .out2(demultiplexer_1_out2),
    .out3(demultiplexer_1_out3), .out4(demultiplexer_1_out4), .out5(demultiplexer_1_out5),
    .out6(demultiplexer_1_out6), .out7(demultiplexer_1_out7), .out8(demultiplexer_1_out8),
    .out9(demultiplexer_1_out9), .out10(demultiplexer_1_out10), .out11(demultiplexer_1_out11),
    .out12(demultiplexer_1_out12), .out13(demultiplexer_1_out13), .out14(demultiplexer_1_out14),
    .out15(demultiplexer_1_out15), .in(data_to_write), .sel(write_port), .en(isWb));
  Multiplexer #(.width(32)) multiplexer_1 (
    .in0({32{1'b1}}), .in1(demultiplexer_1_out14), .out(multiplexer_1_out), .sel(counter_1_q));  // open: en
  not not_1 (not_1_out, counter_1_q);
  Counter #(.width(1), .max('h1), .ongoal("stay")) counter_1 (
    .Q(counter_1_q), .clk(clock), .clr(reset));  // open: load, D, count, carry
  Register #(.width(32)) u_r0 (.D(demultiplexer_1_out0), .en(enbR0), .Q(r0), .clk(clock), .clr(reset));
  Register #(.width(32)) u_r1 (.D(demultiplexer_1_out1), .en(enbR1), .Q(r1), .clk(clock), .clr(reset));
  Register #(.width(32)) u_r2 (.D(demultiplexer_1_out2), .en(enbR2), .Q(r2), .clk(clock), .clr(reset));
  Register #(.width(32)) u_r3 (.D(demultiplexer_1_out3), .en(enbR3), .Q(r3), .clk(clock), .clr(reset));
  Register #(.width(32)) u_r4 (.D(demultiplexer_1_out4), .en(enbR4), .Q(r4), .clk(clock), .clr(reset));
  Register #(.width(32)) u_r5 (.D(demultiplexer_1_out5), .en(enbR5), .Q(r5), .clk(clock), .clr(reset));
  Register #(.width(32)) u_r6 (.D(demultiplexer_1_out6), .en(enbR6), .Q(r6), .clk(clock), .clr(reset));
  Register #(.width(32)) u_r7 (.D(demultiplexer_1_out7), .en(enbR7), .Q(r7), .clk(clock), .clr(reset));
  Register #(.width(32)) u_r8 (.D(demultiplexer_1_out8), .en(enbR8), .Q(r8), .clk(clock), .clr(reset));
  Register #(.width(32)) u_r9 (.D(demultiplexer_1_out9), .en(enbR9), .Q(r9), .clk(clock), .clr(reset));
  Register #(.width(32)) u_r10 (.D(demultiplexer_1_out10), .en(enbR10), .Q(r10), .clk(clock), .clr(reset));
  Register #(.width(32)) u_r11 (.D(demultiplexer_1_out11), .en(enbR11), .Q(r11), .clk(clock), .clr(reset));
  Register #(.width(32)) u_r12 (.D(demultiplexer_1_out12), .en(enbR12), .Q(r12), .clk(clock), .clr(reset));
  Register #(.width(32)) u_r13 (.D(demultiplexer_1_out13), .en(enbR13), .Q(r13), .clk(clock), .clr(reset));
  Register #(.width(32)) u_r14 (.D(multiplexer_1_out), .en(or_1_out), .Q(r14), .clk(clock), .clr(reset));
  or or_1 (or_1_out, not_1_out, enbR14);
  Register #(.width(32)) u_r15 (.D(demultiplexer_1_out15), .en(enbR15), .Q(r15), .clk(clock), .clr(reset));
  Multiplexer #(.select(4), .width(32)) multiplexer_2 (
    .in0(r0), .in1(r1), .in2(r2), .in3(r3), .in4(r4), .in5(r5), .in6(r6), .in7(r7), .in8(r8), .in9(r9),
    .in10(r10), .in11(r11), .in12(r12), .in13(r13), .in14(r14), .in15(r15), .out(op1), .sel(read_port_1));  // open: en
  Multiplexer #(.select(4), .width(32)) multiplexer_3 (
    .in0(r0), .in1(r1), .in2(r2), .in3(r3), .in4(r4), .in5(r5), .in6(r6), .in7(r7), .in8(r8), .in9(r9),
    .in10(r10), .in11(r11), .in12(r12), .in13(r13), .in14(r14), .in15(r15), .out(op2), .sel(read_port_2));  // open: en
endmodule

module ALU (
  input  [31:0] A,
  input  clock,
  input  [31:0] B,
  input  isAdd,
  input  isSub,
  input  isCmp,
  input  isMul,
  input  isDiv,
  input  isMod,
  input  isLsl,
  input  isLsr,
  input  isAsr,
  input  isOr,
  input  isAnd,
  input  isNot,
  input  isMov,
  output GT,
  output E,
  output [31:0] aluResult
);

  wire comparator_1_eq, comparator_1_gt;
  wire [3:0] aluOutputSelect;
  wire [31:0] adder_1_out, and_1_out, divider_1_out, divider_1_rem, multiplier_1_out, not_1_out, or_1_out,
       shifter_1_out, shifter_2_out, shifter_3_out, subtractor_1_out;

  Priority_Encoder #(.select(4)) priority_encoder_1 (
    .in0(isAdd), .in1(isSub), .in2(isMul), .in3(isDiv), .in4(isMod), .in5(isLsl), .in6(isLsr), .in7(isAsr),
    .in8(isOr), .in9(isAnd), .in10(isNot), .in11(isMov), .out(aluOutputSelect));  // open: in12, in13, in14, in15, gs, en_out, en_in
  Adder #(.width(32)) adder_1 (.a(A), .b(B), .out(adder_1_out));  // open: cin, cout
  Subtractor #(.width(32)) subtractor_1 (.a(A), .b(B), .out(subtractor_1_out));  // open: bin, bout
  Multiplier #(.width(32)) multiplier_1 (.a(A), .b(B), .out(multiplier_1_out));  // open: cin, cout
  Divider #(.width(32)) divider_1 (.a(A), .b(B), .out(divider_1_out), .rem(divider_1_rem));  // open: upper
  Shifter #(.width(32)) shifter_1 (.in(A), .\dist (B[4:0]), .out(shifter_1_out));
  Shifter #(.width(32), .shift("lr")) shifter_2 (.in(A), .\dist (B[4:0]), .out(shifter_2_out));
  Shifter #(.width(32), .shift("ar")) shifter_3 (.in(A), .\dist (B[4:0]), .out(shifter_3_out));
  assign or_1_out = A | B;  // OR_Gate or_1, 32 bits wide
  assign and_1_out = A & B;  // AND_Gate and_1, 32 bits wide
  assign not_1_out = ~A;  // NOT_Gate not_1, 32 bits wide
  Comparator #(.width(32)) comparator_1 (.a(A), .b(B), .gt(comparator_1_gt), .eq(comparator_1_eq));  // open: lt
  Register #(.width(1)) register_1 (.D(comparator_1_gt), .en(isCmp), .Q(GT), .clk(clock));  // open: clr
  Register #(.width(1)) register_2 (.D(comparator_1_eq), .en(isCmp), .Q(E), .clk(clock));  // open: clr
  Multiplexer #(.select(4), .width(32)) multiplexer_1 (
    .in0(adder_1_out), .in1(subtractor_1_out), .in2(multiplier_1_out), .in3(divider_1_out),
    .in4(divider_1_rem), .in5(shifter_1_out), .in6(shifter_2_out), .in7(shifter_3_out), .in8(or_1_out),
    .in9(and_1_out), .in10(not_1_out), .in11(B), .out(aluResult), .sel(aluOutputSelect));  // open: in12, in13, in14, in15, en

  // Other names for the same wires on the sheet: shift_by[4:0] = B[4:0]

  // Notes on the sheet:
  //   lsl
  //   lsr
  //   asr
endmodule
